# Fritzing sketch tas-kagit-makas (saved by Fritzing 0.9.2b)
breadboards: 1

parts:
  Part2 = Arduino Uno (Rev3)
  LCD1 = LCD screen  # not connected
  R1 = Resistor [tolerance=±5% resistance=4.7k package=THT]
  R2 = Resistor [tolerance=±5% resistance=4.7k package=THT]
  S1 = Pushbutton [package="[THT]"]
  S2 = Pushbutton [package="[THT]"]
  S3 = Pushbutton [package="[THT]"]

nets:
  N1: Part2.A4/SDA, R2.Pin_0
  N2: Part2.A5/SCL, R1.Pin_0
  N3: Part2.D8, S2.Pin_1, S2.Pin_2
  N4: Part2.D9_PWM, S1.Pin_1, S1.Pin_2
  N5: Part2.D10_PWM/SS, S3.Pin_1, S3.Pin_2
  N6: Part2.GND, R1.Pin_1, R2.Pin_1, S1.Pin_3, S1.Pin_4, S2.Pin_3, S2.Pin_4, S3.Pin_3, S3.Pin_4

notes:
  GND/Vcc/SDA/SDL
