# Fritzing sketch led-blink (saved by Fritzing 0.9.2b)
breadboards: 1

parts:
  Eleman1 = Arduino Uno (Rev3)
  LED2 = smd LED [color="Red (633nm)" package="1206 [SMD]"]
  R1 = Resistor [tolerance=±5% resistance=220 package="2512 [SMD]"]

nets:
  N1: Eleman1.D10_PWM/SS, LED2.cathode
  N2: Eleman1.GND, R1.Pin_1
  N3: LED2.anode, R1.Pin_0
