# Fritzing sketch led-flash (saved by Fritzing 0.9.2b)
breadboards: 1

parts:
  Eleman1 = Arduino Uno (Rev3)
  R1 = Resistor [tolerance=±5% resistance=220 package="2512 [SMD]"]
  R2 = Resistor [tolerance=±5% resistance=220 package="2512 [SMD]"]
  R3 = Resistor [tolerance=±5% resistance=220 package="2512 [SMD]"]
  R4 = Resistor [tolerance=±5% resistance=220 package="2512 [SMD]"]
  R5 = Resistor [tolerance=±5% resistance=220 package="2512 [SMD]"]
  LED1 = LED - 5mm [color="Red (633nm)" package="5 mm [THT]"]
  LED2 = LED - 5mm [color="Red (633nm)" package="5 mm [THT]"]
  LED3 = LED - 5mm [color="Red (633nm)" package="5 mm [THT]"]
  LED4 = LED - 5mm [color="Red (633nm)" package="5 mm [THT]"]
  LED5 = LED - 5mm [color="Red (633nm)" package="5 mm [THT]"]

nets:
  N1: Eleman1.D2, R2.Pin_1
  N2: Eleman1.D3_PWM, R3.Pin_1
  N3: Eleman1.D4, R4.Pin_1
  N4: Eleman1.D5_PWM, R5.Pin_1
  N5: Eleman1.D6_PWM, R1.Pin_1
  N6: Eleman1.GND, LED1.cathode, LED2.cathode, LED3.cathode, LED4.cathode, LED5.cathode
  N7: R1.Pin_0, LED5.anode
  N8: R2.Pin_0, LED1.anode
  N9: R3.Pin_0, LED2.anode
  N10: R4.Pin_0, LED3.anode
  N11: R5.Pin_0, LED4.anode
