# Fritzing sketch i2c-lcd (saved by Fritzing 0.9.2b)
breadboards: 1

parts:
  Part2 = Arduino Uno (Rev3)
  LCD1 = LCD screen  # not connected
  R1 = Resistor [tolerance=±5% resistance=4.7k package=THT]
  R2 = Resistor [tolerance=±5% resistance=4.7k package=THT]

nets:
  N1: Part2.A4/SDA, R2.Pin_1
  N2: Part2.A5/SCL, R1.Pin_1
  N3: Part2.GND, R1.Pin_0, R2.Pin_0

notes:
  GND/Vcc/SDA/SDL
