# Fritzing sketch 7segled-ortak-anot (saved by Fritzing 0.9.2b)
breadboards: 1

parts:
  Part1 = Arduino Uno (Rev3)
  DI1 = 7-Segment LED Display [package=THT]
  R1 = Resistor [tolerance=±5% resistance=220 package=THT]

nets:
  N1: Part1.D8, DI1.cathodeG
  N2: Part1.D2, DI1.cathodeA
  N3: Part1.D3_PWM, DI1.cathodeB
  N4: Part1.D4, DI1.cathodeC
  N5: Part1.D5_PWM, DI1.cathodeD
  N6: Part1.D6_PWM, DI1.cathodeE
  N7: Part1.D7, DI1.cathodeF
  N8: Part1.5V, R1.Pin_1
  N9: DI1.commAnode#7, R1.Pin_0
