# Fritzing sketch 74HC595 (saved by Fritzing 0.9.2b)
breadboards: 1

parts:
  U1 = 74HC595 [package="DIP16 [THT]"]
  LED1 = LED - 5mm [color="Red (633nm)" package="5 mm [THT]"]
  LED2 = smd LED [color="Red (633nm)" package="0805 [SMD]"]
  LED3 = smd LED [color="Red (633nm)" package="0805 [SMD]"]
  LED4 = smd LED [color="Red (633nm)" package="0805 [SMD]"]
  LED5 = smd LED [color="Red (633nm)" package="0805 [SMD]"]
  LED6 = smd LED [color="Red (633nm)" package="0805 [SMD]"]
  LED7 = smd LED [color="Red (633nm)" package="0805 [SMD]"]
  LED8 = smd LED [color="Red (633nm)" package="0805 [SMD]"]
  R2 = Resistor [tolerance=±5% resistance=220 package="0603 [SMD]"]
  R3 = Resistor [tolerance=±5% resistance=220 package="0603 [SMD]"]
  R4 = Resistor [tolerance=±5% resistance=220 package="0603 [SMD]"]
  R5 = Resistor [tolerance=±5% resistance=220 package="0603 [SMD]"]
  R6 = Resistor [tolerance=±5% resistance=220 package="0603 [SMD]"]
  R7 = Resistor [tolerance=±5% resistance=220 package="0603 [SMD]"]
  R8 = Resistor [tolerance=±5% resistance=220 package="0603 [SMD]"]
  R9 = Resistor [tolerance=±5% resistance=220 package="0603 [SMD]"]
  Part1 = Arduino Uno (Rev3) - ICSP

nets:
  N1: U1.Q1, R2.Pin_0
  N2: U1.Q2, R4.Pin_0
  N3: U1.Q3, R5.Pin_0
  N4: U1.Q4, R6.Pin_0
  N5: U1.Q5, R7.Pin_0
  N6: U1.Q6, R8.Pin_0
  N7: U1.Q7, R9.Pin_0
  VCC: U1.MR, U1.VCC, Part1.5V
  N8: U1.SH_CP, Part1.ICSP_MISO, Part1.D12/MISO
  N9: U1.ST_CP, Part1.ICSP_MOSI, Part1.D11_PWM/MOSI
  N10: U1.OE, LED1.cathode, LED2.cathode, LED3.cathode, LED4.cathode, LED5.cathode, LED6.cathode, LED7.cathode, LED8.cathode, Part1.N/C
  N11: U1.DS, Part1.D10_PWM/SS
  N12: LED1.anode, R3.Pin_1
  N13: LED2.anode, R2.Pin_1
  N14: LED3.anode, R4.Pin_1
  N15: LED4.anode, R5.Pin_1
  N16: LED5.anode, R6.Pin_1
  N17: LED6.anode, R7.Pin_1
  N18: LED7.anode, R8.Pin_1
  N19: LED8.anode, R9.Pin_1
